// Logisim project corg-final.circ as structural Verilog: 4 circuits, main circuit main
module main (
  output [15:0] out_1
);

  wire and_1_out, and_2_out, and_3_out, and_4_out, and_5_out, and_6_out, and_7_out, and_8_out, clock_1_out,
       DEC, decoder_1_out0, decoder_1_out3, decoder_1_out5, decoder_5_out0, decoder_5_out1, decoder_5_out2,
       decoder_5_out3, decoder_5_out4, decoder_5_out5, decoder_5_out6, decoder_5_out7, decoder_6_out0,
       decoder_6_out1, decoder_7_out0, decoder_7_out1, decoder_8_out0, decoder_8_out3, decoder_8_out4,
       decoder_8_out5, decoder_8_out6, decoder_8_out7, decoder_11_out0, decoder_11_out1, decoder_12_out0,
       decoder_12_out1, INC, IR_EN, IR_LH, MARTIRH, MARTIRL, MEM_CLR, MEM_LD, MEM_SEL, MEM_STR, MTDST,
       MuxCSel, not_1_out, not_2_out, not_3_out, not_4_out, not_5_out, not_6_out, SRCTDST, SRCTOM;
  wire [1:0] _3RB_FS, _4RB_FS, controlled_buffer_5_out, controlled_buffer_18_out, controlled_buffer_38_out,
       controlled_buffer_39_out, controlled_buffer_44_out, controlled_buffer_47_out,
       controlled_buffer_57_out, controlled_buffer_60_out, controlled_buffer_63_out,
       controlled_buffer_65_out, controlled_buffer_72_out, IR_FS, MuxASel, MuxBSel, OutASel, OutBSel,
       OutCSel, OutDSel;
  wire [2:0] F1, F2, F3;
  wire [3:0] _3RB_RS, _4RB_RS, ALUFlags, ALUFS;

  Decoder #(.select(3), .enable("false")) decoder_1 (
    .out0(decoder_1_out0), .out1(SRCTDST), .out2(MTDST), .out3(decoder_1_out3), .out4(INC),
    .out5(decoder_1_out5), .out6(DEC), .out7(SRCTOM), .sel(F1));
  not not_1 (not_1_out, out_1[10]);
  and and_1 (and_1_out, SRCTDST, not_1_out, not_3_out);
  assign OutASel = and_1_out ? out_1[6:5] : 2'bz;  // Controlled_Buffer controlled_buffer_1
  assign MuxCSel = and_1_out ? 1'b1 : 1'bz;  // Controlled_Buffer controlled_buffer_2
  assign ALUFS = and_1_out ? 4'b0000 : 4'bz;  // Controlled_Buffer controlled_buffer_3
  assign MuxASel = and_1_out ? 2'b11 : 2'bz;  // Controlled_Buffer controlled_buffer_4
  Decoder #(.select(2), .disabled(0)) decoder_2 (
    .out0(_4RB_RS[0]), .out1(_4RB_RS[1]), .out2(_4RB_RS[2]), .out3(_4RB_RS[3]),
    .sel(controlled_buffer_5_out), .en(and_1_out));
  assign controlled_buffer_5_out = and_1_out ? out_1[9:8] : 2'bz;  // Controlled_Buffer controlled_buffer_5
  assign _4RB_FS = and_1_out ? 2'b01 : 2'bz;  // Controlled_Buffer controlled_buffer_6
  assign IR_EN = MARTIRL ? 1'b1 : 1'bz;  // Controlled_Buffer controlled_buffer_7
  assign MEM_SEL = MARTIRL ? 1'b1 : 1'bz;  // Controlled_Buffer controlled_buffer_8
  assign MEM_LD = MARTIRL ? 1'b1 : 1'bz;  // Controlled_Buffer controlled_buffer_9
  assign IR_FS = MARTIRL ? 2'b11 : 2'bz;  // Controlled_Buffer controlled_buffer_10
  assign IR_LH = MARTIRL ? 1'b0 : 1'bz;  // Controlled_Buffer controlled_buffer_11
  assign OutDSel = MARTIRL ? 2'b00 : 2'bz;  // Controlled_Buffer controlled_buffer_12
  assign _3RB_FS = MARTIRL ? 2'b10 : 2'bz;  // Controlled_Buffer controlled_buffer_13
  assign _3RB_RS = MARTIRL ? 4'b0001 : 4'bz;  // Controlled_Buffer controlled_buffer_14
  assign MEM_STR = MARTIRL ? 1'b0 : 1'bz;  // Controlled_Buffer controlled_buffer_15
  assign MEM_CLR = MARTIRL ? 1'b0 : 1'bz;  // Controlled_Buffer controlled_buffer_16
  not not_2 (not_2_out, out_1[10]);
  and and_2 (and_2_out, INC, not_2_out);
  assign _4RB_FS = and_2_out ? 2'b10 : 2'bz;  // Controlled_Buffer controlled_buffer_17
  assign controlled_buffer_18_out = and_2_out ? out_1[9:8] : 2'bz;  // Controlled_Buffer controlled_buffer_18
  assign OutASel = and_2_out ? out_1[9:8] : 2'bz;  // Controlled_Buffer controlled_buffer_19
  assign MuxCSel = and_2_out ? 1'b1 : 1'bz;  // Controlled_Buffer controlled_buffer_20
  assign OutDSel = MTDST ? 2'b01 : 2'bz;  // Controlled_Buffer controlled_buffer_21
  assign MEM_SEL = MTDST ? 1'b1 : 1'bz;  // Controlled_Buffer controlled_buffer_22
  assign MEM_LD = MTDST ? 1'b1 : 1'bz;  // Controlled_Buffer controlled_buffer_23
  assign MEM_STR = MTDST ? 1'b0 : 1'bz;  // Controlled_Buffer controlled_buffer_24
  assign MEM_CLR = MTDST ? 1'b0 : 1'bz;  // Controlled_Buffer controlled_buffer_25
  Clock clock_1 (.out(clock_1_out));
  CONTROL_UNIT control_unit_1 (
    .in_2(out_1[8]), .NEGATIVE_FLAG(ALUFlags[2]), .ZERO_FLAG(ALUFlags[3]), .OPCODE(out_1[15:11]), .F1(F1),
    .F3(F3), .in_1(clock_1_out), .F2(F2));
  not not_3 (not_3_out, out_1[7]);
  Decoder #(.select(2), .disabled(0)) decoder_3 (
    .out0(_4RB_RS[0]), .out1(_4RB_RS[1]), .out2(_4RB_RS[2]), .out3(_4RB_RS[3]),
    .sel(controlled_buffer_18_out), .en(and_2_out));
  assign IR_EN = MARTIRH ? 1'b1 : 1'bz;  // Controlled_Buffer controlled_buffer_26
  assign MEM_SEL = MARTIRH ? 1'b1 : 1'bz;  // Controlled_Buffer controlled_buffer_27
  assign MEM_LD = MARTIRH ? 1'b1 : 1'bz;  // Controlled_Buffer controlled_buffer_28
  assign IR_FS = MARTIRH ? 2'b11 : 2'bz;  // Controlled_Buffer controlled_buffer_29
  assign IR_LH = MARTIRH ? 1'b1 : 1'bz;  // Controlled_Buffer controlled_buffer_30
  assign OutDSel = MARTIRH ? 2'b00 : 2'bz;  // Controlled_Buffer controlled_buffer_31
  assign _3RB_FS = MARTIRH ? 2'b10 : 2'bz;  // Controlled_Buffer controlled_buffer_32
  assign _3RB_RS = MARTIRH ? 4'b0001 : 4'bz;  // Controlled_Buffer controlled_buffer_33
  assign MEM_STR = MARTIRH ? 1'b0 : 1'bz;  // Controlled_Buffer controlled_buffer_34
  assign MEM_CLR = MARTIRH ? 1'b0 : 1'bz;  // Controlled_Buffer controlled_buffer_35
  assign MuxASel = MTDST ? 2'b01 : 2'bz;  // Controlled_Buffer controlled_buffer_36
  assign _4RB_FS = MTDST ? 2'b01 : 2'bz;  // Controlled_Buffer controlled_buffer_37
  assign controlled_buffer_38_out = MTDST ? out_1[10:9] : 2'bz;  // Controlled_Buffer controlled_buffer_38
  and and_3 (and_3_out, SRCTDST, out_1[10], out_1[7]);
  assign controlled_buffer_39_out = and_3_out ? out_1[6:5] : 2'bz;  // Controlled_Buffer controlled_buffer_39
  assign MuxASel = and_3_out ? 2'b10 : 2'bz;  // Controlled_Buffer controlled_buffer_40
  assign MuxCSel = and_3_out ? 1'b0 : 1'bz;  // Controlled_Buffer controlled_buffer_41
  assign ALUFS = and_3_out ? 4'b0000 : 4'bz;  // Controlled_Buffer controlled_buffer_42
  assign MuxBSel = and_3_out ? 2'b11 : 2'bz;  // Controlled_Buffer controlled_buffer_43
  assign controlled_buffer_44_out = and_3_out ? out_1[9:8] : 2'bz;  // Controlled_Buffer controlled_buffer_44
  assign _3RB_FS = and_3_out ? 2'b01 : 2'bz;  // Controlled_Buffer controlled_buffer_45
  Decoder #(.select(2), .disabled(0)) decoder_4 (
    .out0(_4RB_RS[0]), .out1(_4RB_RS[1]), .out2(_4RB_RS[2]), .out3(_4RB_RS[3]),
    .sel(controlled_buffer_38_out), .en(MTDST));
  Decoder #(.select(3), .enable("false")) decoder_5 (
    .out0(decoder_5_out0), .out1(decoder_5_out1), .out2(decoder_5_out2), .out3(decoder_5_out3),
    .out4(decoder_5_out4), .out5(decoder_5_out5), .out6(decoder_5_out6), .out7(decoder_5_out7), .sel(F2));
  outcdecoder outcdecoder_1 (.in_1(controlled_buffer_39_out), .out_2(OutCSel));
  Decoder #(.select(2), .disabled(0)) decoder_6 (
    .out0(decoder_6_out0), .out1(decoder_6_out1), .out2(_3RB_RS[1]), .out3(_3RB_RS[2]),
    .sel(controlled_buffer_44_out), .en(and_3_out));
  or or_1 (_3RB_RS[0], decoder_6_out0, decoder_6_out1);
  and and_4 (and_4_out, INC, out_1[10]);
  assign _3RB_FS = and_4_out ? 2'b10 : 2'bz;  // Controlled_Buffer controlled_buffer_46
  assign controlled_buffer_47_out = and_4_out ? out_1[9:8] : 2'bz;  // Controlled_Buffer controlled_buffer_47
  Decoder #(.select(2), .disabled(0)) decoder_7 (
    .out0(decoder_7_out0), .out1(decoder_7_out1), .out2(_3RB_RS[1]), .out3(_3RB_RS[2]),
    .sel(controlled_buffer_47_out), .en(and_4_out));
  or or_2 (_3RB_RS[0], decoder_7_out0, decoder_7_out1);
  outcdecoder outcdecoder_2 (.in_1(out_1[9:8]), .out_2(OutCSel));
  assign MuxCSel = and_4_out ? 1'b0 : 1'bz;  // Controlled_Buffer controlled_buffer_48
  and and_5 (and_5_out, DEC, not_4_out);
  assign OutBSel = SRCTOM ? out_1[10:9] : 2'bz;  // Controlled_Buffer controlled_buffer_49
  assign ALUFS = SRCTOM ? 4'b0001 : 4'bz;  // Controlled_Buffer controlled_buffer_50
  assign MEM_SEL = SRCTOM ? 1'b1 : 1'bz;  // Controlled_Buffer controlled_buffer_51
  assign MEM_LD = SRCTOM ? 1'b1 : 1'bz;  // Controlled_Buffer controlled_buffer_52
  assign MEM_STR = SRCTOM ? 1'b1 : 1'bz;  // Controlled_Buffer controlled_buffer_53
  assign MEM_CLR = SRCTOM ? 1'b0 : 1'bz;  // Controlled_Buffer controlled_buffer_54
  assign OutDSel = SRCTOM ? 2'b01 : 2'bz;  // Controlled_Buffer controlled_buffer_55
  part2_edited_main main_1 (
    .OutASel(OutASel), .OutBSel(OutBSel), .FunSel_2(_4RB_FS), .RegSel(_4RB_RS), .MuxASel(MuxASel),
    .OutCSel(OutCSel), .OutDSel(OutDSel), .FunSel_3(_3RB_FS), .RegSel_2(_3RB_RS), .L_H(IR_LH),
    .Enable(IR_EN), .FunSel_4(IR_FS), .MuxCSel(MuxCSel), .MuxBSel(MuxBSel), .FunSel(ALUFS), .in_10(MEM_STR),
    .in_11(MEM_SEL), .in_12(MEM_LD), .in_13(MEM_CLR), .out_22(ALUFlags), .out_23(out_1), .in_2(clock_1_out));  // open: out_21
  Decoder #(.select(3), .enable("false")) decoder_8 (
    .out0(decoder_8_out0), .out1(MARTIRL), .out2(MARTIRH), .out3(decoder_8_out3), .out4(decoder_8_out4),
    .out5(decoder_8_out5), .out6(decoder_8_out6), .out7(decoder_8_out7), .sel(F3));
  not not_4 (not_4_out, out_1[10]);
  assign _4RB_FS = and_5_out ? 2'b11 : 2'bz;  // Controlled_Buffer controlled_buffer_56
  Decoder #(.select(2), .disabled(0)) decoder_9 (
    .out0(_4RB_RS[0]), .out1(_4RB_RS[1]), .out2(_4RB_RS[2]), .out3(_4RB_RS[3]),
    .sel(controlled_buffer_57_out), .en(and_5_out));
  assign controlled_buffer_57_out = and_5_out ? out_1[9:8] : 2'bz;  // Controlled_Buffer controlled_buffer_57
  assign OutASel = and_5_out ? out_1[9:8] : 2'bz;  // Controlled_Buffer controlled_buffer_58
  assign MuxCSel = and_5_out ? 1'b1 : 1'bz;  // Controlled_Buffer controlled_buffer_59
  not not_5 (not_5_out, out_1[10]);
  and and_6 (and_6_out, not_5_out, out_1[7]);
  assign controlled_buffer_60_out = and_6_out ? out_1[6:5] : 2'bz;  // Controlled_Buffer controlled_buffer_60
  assign MuxASel = and_6_out ? 2'b10 : 2'bz;  // Controlled_Buffer controlled_buffer_61
  assign _4RB_FS = and_6_out ? 2'b01 : 2'bz;  // Controlled_Buffer controlled_buffer_62
  Decoder #(.select(2), .disabled(0)) decoder_10 (
    .out0(_4RB_RS[0]), .out1(_4RB_RS[1]), .out2(_4RB_RS[2]), .out3(_4RB_RS[3]),
    .sel(controlled_buffer_63_out), .en(and_6_out));
  assign controlled_buffer_63_out = and_6_out ? out_1[9:8] : 2'bz;  // Controlled_Buffer controlled_buffer_63
  Hex_Digit_Display hex_digit_display_1 (.value(out_1[15:12]));  // open: dp
  outcdecoder outcdecoder_3 (.in_1(controlled_buffer_60_out), .out_2(OutCSel));
  Hex_Digit_Display hex_digit_display_2 (.value(out_1[11:8]));  // open: dp
  Hex_Digit_Display hex_digit_display_3 (.value(out_1[7:4]));  // open: dp
  and and_7 (and_7_out, DEC, out_1[10]);
  assign _3RB_FS = and_7_out ? 2'b11 : 2'bz;  // Controlled_Buffer controlled_buffer_64
  assign controlled_buffer_65_out = and_7_out ? out_1[9:8] : 2'bz;  // Controlled_Buffer controlled_buffer_65
  assign MuxCSel = and_7_out ? 1'b0 : 1'bz;  // Controlled_Buffer controlled_buffer_66
  Hex_Digit_Display hex_digit_display_4 (.value(out_1[3:0]));  // open: dp
  and and_8 (and_8_out, SRCTDST, out_1[10], not_6_out);
  assign OutASel = and_8_out ? out_1[6:5] : 2'bz;  // Controlled_Buffer controlled_buffer_67
  assign MuxCSel = and_8_out ? 1'b1 : 1'bz;  // Controlled_Buffer controlled_buffer_68
  assign ALUFS = and_8_out ? 4'b0000 : 4'bz;  // Controlled_Buffer controlled_buffer_69
  assign MuxBSel = and_8_out ? 2'b11 : 2'bz;  // Controlled_Buffer controlled_buffer_70
  assign _3RB_FS = and_8_out ? 2'b01 : 2'bz;  // Controlled_Buffer controlled_buffer_71
  Decoder #(.select(2), .disabled(0)) decoder_11 (
    .out0(decoder_11_out0), .out1(decoder_11_out1), .out2(_3RB_RS[1]), .out3(_3RB_RS[2]),
    .sel(controlled_buffer_72_out), .en(and_8_out));
  assign controlled_buffer_72_out = and_8_out ? out_1[9:8] : 2'bz;  // Controlled_Buffer controlled_buffer_72
  or or_3 (_3RB_RS[0], decoder_11_out0, decoder_11_out1);
  Decoder #(.select(2), .disabled(0)) decoder_12 (
    .out0(decoder_12_out0), .out1(decoder_12_out1), .out2(_3RB_RS[1]), .out3(_3RB_RS[2]),
    .sel(controlled_buffer_65_out), .en(and_7_out));
  or or_4 (_3RB_RS[0], decoder_12_out0, decoder_12_out1);
  outcdecoder outcdecoder_4 (.in_1(out_1[9:8]), .out_2(OutCSel));
  not not_6 (not_6_out, out_1[7]);

  // Other names for the same wires on the sheet: ADDRESS[7:0] = out_1[7:0]; INSTR[15:0] = out_1;
  //   SRCREG2[2:0] = out_1[4:2]; SRCREG1[2:0] = out_1[7:5]; AdrMOD = out_1[8]; DESTREG[2:0] = out_1[10:8];
  //   REGSEL[1:0] = out_1[10:9]; OPCODE[4:0] = out_1[15:11]

  // Notes on the sheet:
  //   MARTIRL
  //   MARTIRH
  //   INC
  //   MTDST
  //   SRCTODST
  //   SRCTOM
  //   DEC
endmodule

module CONTROL_UNIT (
  input  in_1,
  input  in_2,
  input  NEGATIVE_FLAG,
  input  ZERO_FLAG,
  input  [4:0] OPCODE,
  output [2:0] F1,
  output [2:0] F2,
  output [2:0] F3
);

  wire and_1_out, and_2_out, and_3_out, and_4_out, decoder_1_out0, decoder_1_out1, decoder_1_out2,
       decoder_1_out3, multiplexer_1_out, not_1_out, not_2_out;
  wire [1:0] rom_1_data_3, rom_1_data_4;
  wire [2:0] rom_1_data;
  wire [7:0] adder_1_out, controlled_buffer_1_out, controlled_buffer_4_out, register_1_q, register_2_q,
       rom_1_data_2;
  wire [7:2] adder_2_out;

  not not_1 (not_1_out, multiplexer_1_out);
  and and_1 (and_1_out, decoder_1_out0, not_1_out);
  Adder adder_1 (.a(register_1_q), .b(8'h1), .out(adder_1_out));  // open: cin, cout
  assign controlled_buffer_1_out = and_1_out ? adder_1_out : 8'bz;  // Controlled_Buffer controlled_buffer_1
  and and_2 (and_2_out, decoder_1_out0, multiplexer_1_out);
  assign controlled_buffer_1_out = and_2_out ? rom_1_data_2 : 8'bz;  // Controlled_Buffer controlled_buffer_2
  and and_3 (and_3_out, decoder_1_out1, multiplexer_1_out);
  assign controlled_buffer_1_out = and_3_out ? rom_1_data_2 : 8'bz;  // Controlled_Buffer controlled_buffer_3
  assign controlled_buffer_4_out = and_3_out ? adder_1_out : 8'bz;  // Controlled_Buffer controlled_buffer_4
  not not_2 (not_2_out, multiplexer_1_out);
  and and_4 (and_4_out, decoder_1_out1, not_2_out);
  assign controlled_buffer_1_out = and_4_out ? adder_1_out : 8'bz;  // Controlled_Buffer controlled_buffer_5
  Register register_1 (.D(controlled_buffer_1_out), .Q(register_1_q), .clk(in_1));  // open: en, clr
  Register register_2 (.D(controlled_buffer_4_out), .en(and_3_out), .Q(register_2_q), .clk(in_1));  // open: clr
  assign controlled_buffer_1_out = decoder_1_out2 ? register_2_q : 8'bz;  // Controlled_Buffer controlled_buffer_6
  assign controlled_buffer_1_out = decoder_1_out3 ? {adder_2_out, 2'b00} : 8'bz;  // Controlled_Buffer controlled_buffer_7
  ROM #(.dataWidth(24)) rom_1 (
    .addr(register_1_q), .data({F1, F2, F3, rom_1_data_4, rom_1_data_3, rom_1_data_2, rom_1_data}));  // open: sel
  Decoder #(.select(2), .enable("false")) decoder_1 (
    .out0(decoder_1_out0), .out1(decoder_1_out1), .out2(decoder_1_out2), .out3(decoder_1_out3),
    .sel(rom_1_data_3));
  Multiplexer #(.select(2), .enable("false")) multiplexer_1 (
    .in0(1'b1), .in1(in_2), .in2(NEGATIVE_FLAG), .in3(ZERO_FLAG), .out(multiplexer_1_out), .sel(rom_1_data_4));
  Adder #(.width(5)) adder_2 (.a(OPCODE), .b(5'b00001), .out(adder_2_out[6:2]), .cout(adder_2_out[7]));  // open: cin

  // Notes on the sheet:
  //   Control Unit
  //   CAR
  //   SP
  //   Control Memory
  //   contents of rom_1 (hex, n*v repeats v):
  //   8008 10010 1800 0 402030 602030 800 0 e00048 800 0 0 200068 800
  //   IR LOW PLACEHOLDER
endmodule

module outcdecoder (
  input  [1:0] in_1,
  output [1:0] out_2
);

  Subtractor #(.width(2)) subtractor_1 (.a(in_1), .b(2'b01), .out(out_2));  // open: bin, bout
endmodule

module converter (
  input  [2:0] F1,
  input  [2:0] F2,
  input  [2:0] F3,
  input  [1:0] CD,
  input  [1:0] BR,
  input  [7:0] AD,
  input  [2:0] FILLER
);

  wire clock_1_out;
  wire [23:0] ram_1_data;

  // Probe on {F1, F2, F3, CD, BR, AD}
  Clock clock_1 (.out(clock_1_out));
  RAM #(.addrWidth(2), .dataWidth(24), .bus("separate")) ram_1 (
    .addr(2'b00), .din({F1, F2, F3, CD, BR, AD, FILLER}), .data(ram_1_data), .str(1'b1), .clk(clock_1_out),
    .ld(1'b1));  // open: sel, clr
endmodule
